// Logisim project project.circ as structural Verilog: 3 circuits, main circuit main
module main (
  input  [7:0] in_1,
  input  [7:0] in_2,
  input  LOAD,
  input  SEL,
  input  RESET
);

  wire adding_1_sum, adding_2_sum, adding_3_sum, adding_4_sum, adding_5_sum, adding_6_sum, adding_7_sum,
       and_1_out, and_2_out, and_3_out, and_4_out, and_5_out, and_6_out, and_7_out, and_8_out, CLK_out,
       comparator_1_eq, multiplexer_1_out, not_1_out, shift_register_1_out, tcmp_1_out_4;
  wire [4:0] counter_1_q;
  wire [15:0] shift_register_2_q15;

  Shift_Register #(.length(16)) shift_register_1 (
    .clk(multiplexer_1_out), .out(shift_register_1_out), .load(LOAD), .clr(RESET), .d0(in_2[7]),
    .d1(in_2[7]), .d2(in_2[7]), .d3(in_2[7]), .d4(in_2[7]), .d5(in_2[7]), .d6(in_2[7]), .d7(in_2[7]),
    .d8(in_2[7]), .d9(in_2[6]), .d10(in_2[5]), .d11(in_2[4]), .d12(in_2[3]), .d13(in_2[2]), .d14(in_2[1]),
    .d15(in_2[0]));  // open: shift, in, q0, q1, q2, q3, q4, q5, q6, q7, q8, q9, q10, q11, q12, q13, q14, q15
  Multiplexer #(.enable("false")) multiplexer_1 (.in0(LOAD), .in1(CLK_out), .out(multiplexer_1_out), .sel(SEL));
  Clock CLK (.out(CLK_out));
  and and_1 (and_1_out, shift_register_1_out, in_1[7]);
  TCMP tcmp_1 (.X(and_1_out), .RESET(RESET), .out_4(tcmp_1_out_4), .CLK(CLK_out));
  and and_2 (and_2_out, shift_register_1_out, in_1[6]);
  Adding adding_1 (.X(and_2_out), .Sum(adding_1_sum), .Y(tcmp_1_out_4), .RESET(RESET), .CLK(CLK_out));
  and and_3 (and_3_out, shift_register_1_out, in_1[5]);
  and and_4 (and_4_out, shift_register_1_out, in_1[4]);
  Adding adding_2 (.X(and_3_out), .Sum(adding_2_sum), .Y(adding_1_sum), .RESET(RESET), .CLK(CLK_out));
  Adding adding_3 (.X(and_4_out), .Sum(adding_3_sum), .Y(adding_2_sum), .RESET(RESET), .CLK(CLK_out));
  and and_5 (and_5_out, shift_register_1_out, in_1[3]);
  Adding adding_4 (.X(and_5_out), .Sum(adding_4_sum), .Y(adding_3_sum), .RESET(RESET), .CLK(CLK_out));
  and and_6 (and_6_out, in_1[2], shift_register_1_out);
  Adding adding_5 (.X(and_6_out), .Sum(adding_5_sum), .Y(adding_4_sum), .RESET(RESET), .CLK(CLK_out));
  and and_7 (and_7_out, in_1[1], shift_register_1_out);
  Adding adding_6 (.X(and_7_out), .Sum(adding_6_sum), .Y(adding_5_sum), .RESET(RESET), .CLK(CLK_out));
  and and_8 (and_8_out, shift_register_1_out, in_1[0]);
  Adding adding_7 (.X(and_8_out), .Sum(adding_7_sum), .Y(adding_6_sum), .RESET(RESET), .CLK(CLK_out));
  Shift_Register #(.length(16)) shift_register_2 (
    .shift(not_1_out), .in(adding_7_sum), .clk(CLK_out), .clr(RESET), .q0(shift_register_2_q15[15]),
    .q1(shift_register_2_q15[14]), .q2(shift_register_2_q15[13]), .q3(shift_register_2_q15[12]),
    .q4(shift_register_2_q15[11]), .q5(shift_register_2_q15[10]), .q6(shift_register_2_q15[9]),
    .q7(shift_register_2_q15[8]), .q8(shift_register_2_q15[7]), .q9(shift_register_2_q15[6]),
    .q10(shift_register_2_q15[5]), .q11(shift_register_2_q15[4]), .q12(shift_register_2_q15[3]),
    .q13(shift_register_2_q15[2]), .q14(shift_register_2_q15[1]), .q15(shift_register_2_q15[0]));  // open: out, load, d0, d1, d2, d3, d4, d5, d6, d7, d8, d9, d10, d11, d12, d13, d14, d15
  Counter #(.width(5), .max('h11), .ongoal("stay")) counter_1 (
    .Q(counter_1_q), .clk(CLK_out), .clr(RESET));  // open: load, D, count, carry
  // Probe on shift_register_2_q15
  Comparator #(.width(5), .mode("unsigned")) comparator_1 (
    .a(counter_1_q), .b(5'b10001), .eq(comparator_1_eq));  // open: gt, lt
  not not_1 (not_1_out, comparator_1_eq);
endmodule

module Adding (
  input  X,
  input  Y,
  input  RESET,
  input  CLK,
  output Sum
);

  wire adder_1_cout, adder_1_out, and_1_out, and_2_out, d_ff_2_q, xor_1_out, xor_2_out;

  Adder #(.width(1)) adder_1 (.a(Y), .b(d_ff_2_q), .out(adder_1_out), .cout(adder_1_cout));  // open: cin
  and and_1 (and_1_out, X, adder_1_out);
  xor xor_1 (xor_1_out, X, adder_1_out);
  D_Flip_Flop d_ff_1 (.clk(CLK), .D(xor_1_out), .Q(Sum), .reset(RESET));  // open: Qn, preset, en
  xor xor_2 (xor_2_out, and_1_out, adder_1_cout);
  and and_2 (and_2_out, and_1_out, adder_1_cout);
  D_Flip_Flop d_ff_2 (.clk(CLK), .D(xor_2_out), .Q(d_ff_2_q), .reset(RESET));  // open: Qn, preset, en
endmodule

module TCMP (
  input  X,
  input  CLK,
  input  RESET,
  output out_4
);

  wire and_1_out, d_ff_2_q, or_1_out, xor_1_out;

  xor xor_1 (xor_1_out, X, d_ff_2_q);
  and and_1 (and_1_out, X, d_ff_2_q);
  D_Flip_Flop d_ff_1 (.clk(CLK), .D(xor_1_out), .Q(out_4), .reset(RESET));  // open: Qn, preset, en
  or or_1 (or_1_out, X, d_ff_2_q);
  D_Flip_Flop d_ff_2 (.clk(CLK), .D(or_1_out), .Q(d_ff_2_q), .reset(RESET));  // open: Qn, preset, en
endmodule
